# Fritzing sketch example1_sketch (saved by Fritzing 0.9.3b)
breadboards: 1

parts:
  5VDC = Header 2 [package=molex-1x2_lock]
  WeMos_D1_Mini_Relay_Shield_V1 = WeMos D1 Mini Relay Shield V2  # not connected
  WeMos_D1_Mini1 = WeMos D1 Mini
  WeMos_D1_Mini_Relay_Shield_V2 = WeMos D1 Mini Relay Shield V2  # not connected
  WeMos_D1_Mini_Relay_Shield_V3 = WeMos D1 Mini Relay Shield V2  # not connected
  WeMos_D1_Mini_Relay_Shield_V4 = WeMos D1 Mini Relay Shield V2  # not connected

nets:
  N1: 5VDC.1, WeMos_D1_Mini1.5V
  N2: 5VDC.2, WeMos_D1_Mini1.G

notes:
  5V
